# Fritzing sketch kytkennät (saved by Fritzing 0.9.1b)

parts:
  Part1 = Arduino Pro Mini v13
  LED1 = LED - 3mm [color="Red (633nm)" package="3 mm [THT]"]
  R1 = Photocell (LDR) [package=THT]
  R2 = Resistor [tolerance=±5% resistance=4.7k package=THT]
  NRF24L1 = NRF24L01
  Part2 = Arduino Pro Mini v13
  LED2 = LED - 3mm [color="Red (633nm)" package="3 mm [THT]"]
  NRF24L2 = NRF24L01
  Part3 = Arduino Pro Mini v13
  J1 = female pin header, 8 pins [form="♀ (female)"]
  U1 = LIPO-150mAh [package=lipo-150]
  U2 = LIPO-150mAh [package=lipo-150]

nets:
  VCC: Part1.VCC, R2.Pin_0, NRF24L1.VCC, U2.+
  GND: Part1.GND, LED1.cathode, R1.pin_0, NRF24L1.GND, U2.-
  N1: Part1.A0, R1.pin_1, R2.Pin_1
  N2: Part1.D13/SCK, NRF24L1.SCK
  N3: Part1.D12/MISO, NRF24L1.MISO
  N4: Part1.D11_PWM/MOSI, NRF24L1.MOSI
  N5: Part1.D10_PWM/SS, NRF24L1.CSN
  N6: Part1.D9_PWM, NRF24L1.CE
  N7: Part1.D3_PWM, LED1.anode
  N8: Part2.D3_PWM, LED2.anode
  N9: Part2.GND, LED2.cathode
  VCC_2: NRF24L2.VCC, Part3.VCC, J1.pin6
  N10: NRF24L2.CSN, Part3.D10_PWM/SS
  N11: NRF24L2.MOSI, Part3.D11_PWM/MOSI
  GND_2: NRF24L2.GND, Part3.GND, J1.pin8, U1.-
  N12: NRF24L2.CE, Part3.D9_PWM
  N13: NRF24L2.SCK, Part3.D13/SCK
  N14: NRF24L2.MISO, Part3.D12/MISO
  N15: Part3.RAW, U1.+
  N16: Part3.D7, J1.pin5
  N17: Part3.D6_PWM, J1.pin4, J1.pin7
  N18: Part3.D5_PWM, J1.pin3
  N19: Part3.D4, J1.pin2
  N20: Part3.D3_PWM, J1.pin1

custom parts:
  NRF24L01: NRF24L01 module
  LIPO-150mAh: 150mAh Lipo-battery
